# Fritzing sketch esupnfctagarduino (saved by Fritzing 0.9.3b)

parts:
  LCD2 = LCD screen
  LCM1602_IIC2 = LCM1602 IIC [part_number="LCM1602 IIC" chip_label="LCM1602 IIC" package="DIP (Dual Inline) [THT]"]
  Composant3 = Arduino Uno (Rev3)
  J1 = Piezo Speaker
  LED3 = Super Flux RGB LED (com. cathode)
  Composant5 = ITEAD PN532 NFC Module
  Composant7 = W5100 MODULE

nets:
  VSS: LCD2.VSS, LCM1602_IIC2.VSS
  VDD: LCD2.VDD, LCM1602_IIC2.VDD
  N1: LCD2.V0, LCM1602_IIC2.V0
  N2: LCD2.RS, LCM1602_IIC2.RS
  N3: LCD2.R/W, LCM1602_IIC2.RW
  N4: LCD2.E, LCM1602_IIC2.E
  N5: LCD2.DB0, LCM1602_IIC2.D0
  N6: LCD2.DB1, LCM1602_IIC2.D1
  N7: LCD2.DB2, LCM1602_IIC2.D2
  N8: LCD2.DB3, LCM1602_IIC2.D3
  N9: LCD2.DB4, LCM1602_IIC2.D4
  N10: LCD2.DB5, LCM1602_IIC2.D5
  N11: LCD2.DB6, LCM1602_IIC2.D6
  N12: LCD2.DB7, LCM1602_IIC2.D7
  N13: LCD2.LED+, LCM1602_IIC2.A
  N14: LCD2.LED-, LCM1602_IIC2.K
  GND: LCM1602_IIC2.GND, Composant3.GND, J1.pin1, LED3.common_cathode, Composant5.GND, Composant7.GND
  5V: LCM1602_IIC2.VCC, Composant3.5V, Composant5.5V
  N15: LCM1602_IIC2.SDA, Composant3.A4/SDA
  N16: LCM1602_IIC2.SCL, Composant3.A5/SCL
  N17: LCM1602_IIC2.LED_A, LCM1602_IIC2.LED_B
  N18: Composant3.D8, LED3.red_anode
  N19: Composant3.D9_PWM, LED3.green_anode
  N20: Composant3.D10_PWM/SS, Composant7.NSS
  N21: Composant3.D11_PWM/MOSI, Composant7.MO
  N22: Composant3.D12/MISO, Composant7.MI
  N23: Composant3.D13/SCK, Composant7.SCK
  N24: Composant3.D2, Composant5.SCK#12
  N25: Composant3.D3_PWM, Composant5.MO/SDA/TX
  N26: Composant3.D4, Composant5.NSS/SCL/RX, Composant5.SCK#49
  N27: Composant3.D5_PWM, Composant5.MI
  N28: Composant3.D6_PWM, J1.pin2
  N29: Composant3.ioref, Composant7.VDD

notes:
  PN532
  W5100

custom parts:
  LCM1602 IIC: I2C-Module to use a 1602 or 2004 LCD on with the wire.h libory Serial LCD Modul
  ITEAD PN532 NFC Module: Breakout board Platform Based On Arduino by Iteadstudio Principal features : Electronic Brick Ports 3.3V or 5V power supply The official support forum: support@iteadstudio.com
  W5100 MODULE: The official support forum: support@iteadstudio.com
